# Fritzing sketch 12v Battery pack connection (saved by Fritzing 0.9.8b)

parts:
  U1 = PIC-ICSP [package=molex-1x6_lock]
  BAT1 = 18650 battery holder [package=battery-18650-kit]
  BAT2 = 18650 battery holder [package=battery-18650-kit]
  BAT3 = 18650 battery holder [package=battery-18650-kit]

nets:
  N1: U1.B-, BAT3.-
  N2: U1.B+, BAT1.+
  N3: BAT1.-, BAT2.+
  N4: BAT2.-, BAT3.+

custom parts:
  PIC-ICSP: ISCP Programming connector for UAV, UBW Kit, etc.
  18650 battery holder: 18650 Battery Holder
